// Logisim project Laba4D2481.circ as structural Verilog: 1 circuit, main circuit main
// 10unsigned
module main (
  input  [3:0] D8421,
  output [3:0] D8421_2
);

  wire not_1_out, not_2_out, not_3_out, or_1_out, or_2_out, or_4_out, or_5_out, or_6_out, or_7_out, or_8_out;

  // Probe on D8421
  not not_1 (not_1_out, D8421[1]);
  not not_2 (not_2_out, D8421[2]);
  not not_3 (not_3_out, D8421[1]);
  or or_1 (or_1_out, D8421[3], D8421[0]);
  and and_1 (D8421_2[0], or_1_out, or_2_out);
  or or_2 (or_2_out, D8421[2], D8421[1], D8421[0]);
  or or_3 (D8421_2[1], D8421[3], not_1_out);
  or or_4 (or_4_out, D8421[2], D8421[1], D8421[0]);
  or or_5 (or_5_out, D8421[3], not_2_out, not_3_out);
  or or_6 (or_6_out, D8421[3], D8421[2], D8421[1]);
  or or_7 (or_7_out, D8421[3], D8421[2]);
  or or_8 (or_8_out, D8421[3], D8421[1]);
  and and_2 (D8421_2[2], or_4_out, or_5_out, or_6_out);
  and and_3 (D8421_2[3], or_7_out, or_8_out);
  // Probe on D8421_2
endmodule
