// Logisim project diagram3.circ as structural Verilog: 1 circuit, main circuit main
module main (
  input  [7:0] in_1,
  input  [7:0] in_2,
  output [7:0] out_3
);

  wire and_1_out, and_2_out, and_3_out, and_4_out, and_5_out, and_6_out, and_7_out, and_8_out, and_9_out,
       and_10_out, and_11_out, and_12_out, and_13_out, and_14_out, and_15_out, and_16_out, xor_1_out,
       xor_2_out, xor_3_out, xor_4_out, xor_5_out, xor_6_out, xor_7_out, xor_8_out, xor_17_out, xor_18_out,
       xor_19_out, xor_20_out, xor_21_out, xor_22_out, xor_23_out, xor_24_out;

  // Probe on in_2
  // Probe on in_1
  xor xor_1 (xor_1_out, in_1[0], in_2[0]);
  xor xor_2 (xor_2_out, in_1[1], in_2[1]);
  xor xor_3 (xor_3_out, in_1[2], in_2[2]);
  xor xor_4 (xor_4_out, in_1[3], in_2[3]);
  xor xor_5 (xor_5_out, in_1[4], in_2[4]);
  xor xor_6 (xor_6_out, in_1[5], in_2[5]);
  xor xor_7 (xor_7_out, in_1[6], in_2[6]);
  xor xor_8 (xor_8_out, in_1[7], in_2[7]);
  xor xor_9 (out_3[0], xor_1_out, 1'b0);
  and and_1 (and_1_out, xor_1_out, 1'b0);
  and and_2 (and_2_out, in_1[0], in_2[0]);
  xor xor_10 (out_3[1], xor_2_out, xor_17_out);
  and and_3 (and_3_out, xor_2_out, xor_17_out);
  and and_4 (and_4_out, in_1[1], in_2[1]);
  xor xor_11 (out_3[2], xor_3_out, xor_18_out);
  and and_5 (and_5_out, xor_3_out, xor_18_out);
  and and_6 (and_6_out, in_1[2], in_2[2]);
  xor xor_12 (out_3[3], xor_4_out, xor_19_out);
  and and_7 (and_7_out, xor_4_out, xor_19_out);
  and and_8 (and_8_out, in_1[3], in_2[3]);
  xor xor_13 (out_3[4], xor_5_out, xor_20_out);
  and and_9 (and_9_out, xor_5_out, xor_20_out);
  and and_10 (and_10_out, in_1[4], in_2[4]);
  xor xor_14 (out_3[5], xor_6_out, xor_21_out);
  and and_11 (and_11_out, xor_6_out, xor_21_out);
  and and_12 (and_12_out, in_1[5], in_2[5]);
  xor xor_15 (out_3[6], xor_7_out, xor_22_out);
  and and_13 (and_13_out, xor_7_out, xor_22_out);
  and and_14 (and_14_out, in_1[6], in_2[6]);
  xor xor_16 (out_3[7], xor_8_out, xor_23_out);
  and and_15 (and_15_out, xor_8_out, xor_23_out);
  and and_16 (and_16_out, in_1[7], in_2[7]);
  xor xor_17 (xor_17_out, and_1_out, and_2_out);
  xor xor_18 (xor_18_out, and_3_out, and_4_out);
  xor xor_19 (xor_19_out, and_5_out, and_6_out);
  xor xor_20 (xor_20_out, and_7_out, and_8_out);
  xor xor_21 (xor_21_out, and_9_out, and_10_out);
  xor xor_22 (xor_22_out, and_11_out, and_12_out);
  xor xor_23 (xor_23_out, and_13_out, and_14_out);
  xor xor_24 (xor_24_out, and_15_out, and_16_out);
  // Probe on out_3
  // also tied to GND on the sheet: xor_24_out
endmodule
