// Logisim project difference.circ as structural Verilog: 1 circuit, main circuit main
module main (
  input  V,
  output out_2,
  output out_3,
  output out_4
);

  wire and_1_out, and_2_out, clock_1_out, not_1_out, not_2_out;

  and and_1 (and_1_out, not_1_out, not_2_out, V);
  not not_1 (not_1_out, out_3);
  and and_2 (and_2_out, V, not_2_out);
  not not_2 (not_2_out, out_4);
  Clock clock_1 (.out(clock_1_out));
  T_Flip_Flop t_ff_1 (.clk(clock_1_out), .T(and_1_out), .Q(out_2));  // open: Qn, preset, reset, en
  T_Flip_Flop t_ff_2 (.clk(clock_1_out), .T(and_2_out), .Q(out_3));  // open: Qn, preset, reset, en
  T_Flip_Flop t_ff_3 (.clk(clock_1_out), .T(V), .Q(out_4));  // open: Qn, preset, reset, en

  // Notes on the sheet:
  //   !q2*
  //   !q1*
  //   V
  //   V
  //   !q1*
  //   !q2*
  //   !q1*
  //   q3*
  //   q2*
  //   q1*
endmodule
