// Logisim project Laba4Sum1.circ as structural Verilog: 2 circuits, main circuit 8bitSum
module oniBitMin (
  input  a,
  input  b,
  input  p,
  output P_2,
  output S
);

  wire not_1_out, not_2_out, not_3_out, or_1_out, or_2_out, or_3_out, or_4_out, or_5_out, or_6_out, or_7_out;

  not not_1 (not_1_out, a);
  not not_2 (not_2_out, b);
  not not_3 (not_3_out, p);
  or or_1 (or_1_out, a, p);
  or or_2 (or_2_out, b, p);
  or or_3 (or_3_out, a, b);
  or or_4 (or_4_out, a, b, p);
  or or_5 (or_5_out, not_1_out, not_2_out, p);
  or or_6 (or_6_out, a, not_2_out, not_3_out);
  or or_7 (or_7_out, not_1_out, b, not_3_out);
  and and_1 (P_2, or_1_out, or_2_out, or_3_out);
  and and_2 (S, or_4_out, or_5_out, or_6_out, or_7_out);
endmodule

module _8bitSum (
  input  [7:0] in_1,
  input  in_2,
  input  [7:0] in_3,
  output [7:0] out_4
);

  wire onibitmin_1_p_2, onibitmin_2_p_2, onibitmin_3_p_2, onibitmin_4_p_2, onibitmin_5_p_2, onibitmin_6_p_2,
       onibitmin_7_p_2;

  // Probe on in_3
  // Probe on in_1
  oniBitMin onibitmin_1 (.a(in_1[0]), .b(in_3[0]), .p(in_2), .P_2(onibitmin_1_p_2), .S(out_4[0]));
  oniBitMin onibitmin_2 (.a(in_1[1]), .b(in_3[1]), .p(onibitmin_1_p_2), .P_2(onibitmin_2_p_2), .S(out_4[1]));
  oniBitMin onibitmin_3 (.a(in_1[2]), .b(in_3[2]), .p(onibitmin_2_p_2), .P_2(onibitmin_3_p_2), .S(out_4[2]));
  oniBitMin onibitmin_4 (.a(in_1[3]), .b(in_3[3]), .p(onibitmin_3_p_2), .P_2(onibitmin_4_p_2), .S(out_4[3]));
  oniBitMin onibitmin_5 (.a(in_1[4]), .b(in_3[4]), .p(onibitmin_4_p_2), .P_2(onibitmin_5_p_2), .S(out_4[4]));
  oniBitMin onibitmin_6 (.a(in_1[5]), .b(in_3[5]), .p(onibitmin_5_p_2), .P_2(onibitmin_6_p_2), .S(out_4[5]));
  oniBitMin onibitmin_7 (.a(in_1[6]), .b(in_3[6]), .p(onibitmin_6_p_2), .P_2(onibitmin_7_p_2), .S(out_4[6]));
  oniBitMin onibitmin_8 (.a(in_1[7]), .b(in_3[7]), .p(onibitmin_7_p_2), .S(out_4[7]));  // open: P_2
  // Probe on out_4
endmodule
